# Fritzing sketch protype1 (saved by Fritzing 0.9.3b)
circuit board: 8.46667cm x 5.64444cm
breadboards: 1

parts:
  Q1 = NPN-Transistor [package="TO92 [THT]"]
  Q6 = PNP-Transistor [package="TO92 [THT]"]
  Q3 = NPN-Transistor [package="TO92 [THT]"]  # not connected
  Q5 = PNP-Transistor [package="TO92 [THT]"]
  R1 = Resistor [tolerance=±5% resistance=2k package=THT]
  R2 = Resistor [tolerance=±5% resistance=100k package=THT]
  R3 = Resistor [tolerance=±5% resistance=3.9k package=THT]
  R4 = Resistor [tolerance=±5% resistance=100k package=THT]
  R5 = Resistor [tolerance=±5% resistance=3.9k package=THT]
  LED1 = LED - 5mm [color="Red (633nm)" package="5 mm [THT]"]
  LED2 = LED - 5mm [color="Red (633nm)" package="5 mm [THT]"]
  Q4 = NPN-Transistor [package="TO92 [THT]"]
  Q2 = NPN-Transistor [package="TO92 [THT]"]
  R6 = Resistor [tolerance=±5% resistance=3.9k package=THT]
  R7 = Resistor [tolerance=±5% resistance=3.9k package=THT]
  J1 = female pin header, 2 pins [form="♀ (female)"]
  J2 = female pin header, 2 pins [form="♀ (female)"]

nets:
  GND: Q1.E, Q4.E, Q2.E
  N1: Q1.B, R5.Pin_1
  N2: Q1.C, Q6.C, J2.pin1
  30V: Q6.E, Q5.E
  N3: Q6.B, R4.Pin_1
  N4: Q5.B, R2.Pin_0
  N5: Q5.C, J1.pin2
  N6: R1.Pin_0, LED1.anode, LED2.cathode
  N7: R1.Pin_1, J1.pin1
  N8: R2.Pin_1, Q2.C
  GPIO22: R3.Pin_1
  N9: R4.Pin_0, Q4.C
  GPIO17: R5.Pin_0
  N10: LED1.cathode, LED2.anode, J2.pin2
  N11: Q4.B, R6.Pin_1
  N12: Q2.B, R7.Pin_0
  GPIO23: R6.Pin_0
  GPIO18: R7.Pin_1
